# Fritzing sketch watt (saved by Fritzing 0.9.6b)

parts:
  INA1 = INA219 DC Current Sensor Breakout
  Mod1 = Raspberry Pi Pico
  IC1 = LM324 [package=dil16]
  Power_plug1 = USB-C plug
  JACK1 = 2.1mm Barrel Jack with Terminal Block
  R1 = Resistor [tolerance=±5% power=0.25 resistance=3.3k package=THT]
  R2 = Resistor [tolerance=±5% power=0.25 resistance=22k package=THT]
  R3 = Resistor [tolerance=±5% power=0.25 resistance=1k package=THT]
  R4 = Resistor [tolerance=±5% power=0.25 resistance=1.5k package=THT]
  R6 = Resistor [tolerance=±5% power=0.25 resistance=2.2k package=THT]
  R7 = Resistor [tolerance=±5% power=0.25 resistance=2.2k package=THT]
  Mod2 = Raspberry Pi 4B  # not connected

nets:
  N1: INA1.VCC, Mod1.pin_36
  GND: INA1.GND, Mod1.pin_18, Mod1.pin_23, Mod1.pin_33, Mod1.pin_42, IC1.IN3-, IC1.GND, R3.Pin_1, R4.Pin_1
  N2: INA1.SCL, Mod1.pin_22
  N3: INA1.SDA, Mod1.pin_21
  N4: INA1.Vin-, Power_plug1.VCC, R7.Pin_1
  N5: INA1.Vin+, JACK1.POS
  N6: Mod1.pin_31, IC1.OUT1, R2.Pin_0
  N7: Mod1.pin_40, IC1.V+, R1.Pin_1
  N8: IC1.IN1-, R2.Pin_1, R6.Pin_0
  N9: Power_plug1.GND, JACK1.NEG
  N10: R1.Pin_0, R4.Pin_0, R6.Pin_1
  N11: R3.Pin_0, R7.Pin_0

notes:
  +5V 3A
  Serial Data
  Data Collection PC
  Power to Raspberry pi 4b
  Input power
  Custom wattmeter

custom parts:
  INA219 DC Current Sensor Breakout: INA DC Current Sensor Breakout
  Raspberry Pi Pico: Raspberry Pi Pico. Based around the RP2040 microcontroller the Pico is a low cost microcontroller device bringing Raspberry Pi quality, cost, and easy of use to the microcontroller space. Jan 2021, Split part in to two versions: tht (this one) and SMD. This one will drill holes for a .1 in header in pcb to allow plugging in the module as well as providing pads to solder the module to the top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
  LM324: LM324 Quad OpAmp
  USB-C plug: power plug
